// Logisim project Project4Given.circ as structural Verilog: 7 circuits, main circuit NIC
module main (
  input  En_Noise
);

  wire CLK, keyboard_1_avail, multiplexer_1_out, nic_1_int, nic_1_tx, noisychannel_1_out,
       terminalcontroller_1_cs, terminalcontroller_1_kben, terminalcontroller_1_o,
       terminalcontroller_1_ttyen, terminalcontroller_1_w;
  wire [1:0] terminalcontroller_1_addr;
  wire [6:0] keyboard_1_data, terminalcontroller_1_ttydata;
  wire [7:0] nic_1_dataout, terminalcontroller_1_dataout, terminalcontroller_1_status;

  TTY tty_1 (.data(terminalcontroller_1_ttydata), .clk(CLK), .we(terminalcontroller_1_ttyen));  // open: clr
  Keyboard keyboard_1 (
    .clk(CLK), .re(terminalcontroller_1_kben), .avail(keyboard_1_avail), .data(keyboard_1_data));  // open: clr
  LED DR (.in(terminalcontroller_1_status[1]));
  LED TBNF (.in(terminalcontroller_1_status[2]));
  LED TXI (.in(terminalcontroller_1_status[3]));
  LED NF (.in(terminalcontroller_1_status[4]));
  LED OR (.in(terminalcontroller_1_status[5]));
  LED SDE (.in(terminalcontroller_1_status[6]));
  LED FE (.in(terminalcontroller_1_status[7]));
  Clock clock_1 (.out(CLK));
  TerminalController terminalcontroller_1 (
    .TTYEN(terminalcontroller_1_ttyen), .TTYDATA(terminalcontroller_1_ttydata),
    .STATUS(terminalcontroller_1_status), .KBEN(terminalcontroller_1_kben), .KBRDY(keyboard_1_avail),
    .KBDATA(keyboard_1_data), .CLK(CLK), .DIV(4'b0011), .INT(nic_1_int), .CS(terminalcontroller_1_cs),
    .O(terminalcontroller_1_o), .W(terminalcontroller_1_w), .ADDR(terminalcontroller_1_addr),
    .DATAOUT(terminalcontroller_1_dataout), .DATAIN(nic_1_dataout));
  NIC nic_1 (
    .INT(nic_1_int), .CS(terminalcontroller_1_cs), .O(terminalcontroller_1_o), .W(terminalcontroller_1_w),
    .ADDR(terminalcontroller_1_addr), .DATAIN(terminalcontroller_1_dataout), .DATAOUT(nic_1_dataout),
    .CLK(CLK), .TX(nic_1_tx), .RX(multiplexer_1_out));
  Shift_Register #(.length(32)) shift_register_1 (
    .in(nic_1_tx), .clk(CLK));  // open: shift, out, load, clr, d0, q0, d1, q1, d2, q2, d3, q3, d4, q4, d5, q5, d6, q6, d7, q7, d8, q8, d9, q9, d10, q10, d11, q11, d12, q12, d13, q13, d14, q14, d15, q15, d16, q16, d17, q17, d18, q18, d19, q19, d20, q20, d21, q21, d22, q22, d23, q23, d24, q24, d25, q25, d26, q26, d27, q27, d28, q28, d29, q29, d30, q30, d31, q31
  Shift_Register #(.length(32)) shift_register_2 (
    .in(multiplexer_1_out), .clk(CLK));  // open: shift, out, load, clr, d0, q0, d1, q1, d2, q2, d3, q3, d4, q4, d5, q5, d6, q6, d7, q7, d8, q8, d9, q9, d10, q10, d11, q11, d12, q12, d13, q13, d14, q14, d15, q15, d16, q16, d17, q17, d18, q18, d19, q19, d20, q20, d21, q21, d22, q22, d23, q23, d24, q24, d25, q25, d26, q26, d27, q27, d28, q28, d29, q29, d30, q30, d31, q31
  NoisyChannel noisychannel_1 (.In(nic_1_tx), .Rate(16'h800), .CLK(CLK), .Out(noisychannel_1_out));
  Multiplexer #(.enable("false")) multiplexer_1 (
    .in0(nic_1_tx), .in1(noisychannel_1_out), .out(multiplexer_1_out), .sel(En_Noise));

  // Notes on the sheet:
  //   Div
  //   Noise Rate
endmodule

module TerminalController (
  input  KBRDY,
  input  [6:0] KBDATA,
  input  INT,
  input  [7:0] DATAIN,
  input  CLK,
  input  [3:0] DIV,
  output KBEN,
  output CS,
  output O,
  output TTYEN,
  output W,
  output [6:0] TTYDATA,
  output [1:0] ADDR,
  output [7:0] STATUS,
  output [7:0] DATAOUT
);

  wire DOCHECKS, JMP, not_4_out, not_5_out, not_6_out, STATUSEN, TF, TTYDATAOUTSEL, TTYENP;
  wire [1:0] and_2_out, DATAOUTSEL;
  wire [7:0] DATABUSBYTE, INST, JUMPTARGET, multiplexer_1_out, multiplexer_3_out;
  wire [7:7] multiplexer_2_out;
  wire [23:11] rom_1_data;

  ROM #(.dataWidth(24)) rom_1 (
    .addr(INST),
    .data({rom_1_data[23:21], ADDR, KBEN, TTYENP, DATAOUTSEL, TTYDATAOUTSEL, rom_1_data[13:11], DOCHECKS, STATUSEN, JMP, DATABUSBYTE}),
    .sel(1'b1));
  not not_1 (W, rom_1_data[21]);
  not not_2 (O, rom_1_data[22]);
  not not_3 (CS, rom_1_data[23]);
  Multiplexer #(.select(2), .width(8), .enable("false")) multiplexer_1 (
    .in0({4'b0000, DIV}), .in1(DATABUSBYTE), .in2({1'b1, KBDATA}), .in3({8{1'b0}}), .out(multiplexer_1_out),
    .sel(DATAOUTSEL));
  assign DATAOUT = not_4_out ? multiplexer_1_out : 8'bz;  // Controlled_Buffer controlled_buffer_1
  not not_4 (not_4_out, W);
  Multiplexer #(.width(8), .enable("false")) multiplexer_2 (
    .in0(DATAIN), .in1(DATABUSBYTE), .out({multiplexer_2_out[7], TTYDATA}), .sel(TTYDATAOUTSEL));
  and and_1 (TTYEN, multiplexer_2_out[7], TTYENP);
  Counter counter_1 (.load(JMP), .D(JUMPTARGET), .count(not_5_out), .Q(INST), .clk(CLK));  // open: carry, clr
  not not_5 (not_5_out, JMP);
  Multiplexer #(.width(8), .enable("false")) multiplexer_3 (
    .in0(8'h20), .in1(8'h30), .out(multiplexer_3_out), .sel(TF));
  and and_2 (and_2_out[0], KBRDY, DOCHECKS);
  and and_3 (and_2_out[1], DOCHECKS, not_6_out);
  not not_6 (not_6_out, INT);
  Comparator #(.width(7), .mode("unsigned")) comparator_1 (.a(KBDATA), .b(7'b0001010), .eq(TF));  // open: gt, lt
  Register register_1 (.D(DATAIN), .en(STATUSEN), .Q(STATUS), .clk(CLK));  // open: clr
  Multiplexer #(.select(2), .width(8), .enable("false")) multiplexer_4 (
    .in0(DATABUSBYTE), .in1(multiplexer_3_out), .in2(8'h10), .in3(8'h10), .out(JUMPTARGET), .sel(and_2_out));

  // Other names for the same wires on the sheet: KBDATABUSBYTE[6:0] = KBDATA

  // Notes on the sheet:
  //   contents of rom_1 (hex, n*v repeats v):
  //   0 b80000 b80000 0 a88002 a88002 0 a08001 a08001 0 c00000 c00000 c00200 509 0 0 d00000 d00000 d20000
  //   109 12*0 b10000 b10000 b10000 40000 109 11*0 b10000 b10000 b10000 40000 a08003 a08003 109
endmodule

module NIC (
  input  CS,
  input  O,
  input  W,
  input  RX,
  input  [1:0] ADDR,
  input  [7:0] DATAIN,
  input  CLK,
  output INT,
  output TX,
  output [7:0] DATAOUT
);

  ClockDivisor clockdivisor_1 (.in_1(CLK));  // open: in_2, out_3, out_4, out_5, out_6, out_7, out_8, out_9, out_10, out_11, out_12, out_13, out_14, out_15
endmodule

module NoisyChannel (
  input  [15:0] Rate,
  input  In,
  input  CLK,
  output Out
);

  wire Flip;
  wire [15:0] RNG;
  wire [31:0] adder_1_out, multiplier_1_out, SEED;

  xor xor_1 (Out, In, Flip);
  Multiplier #(.width(32)) multiplier_1 (.a(SEED), .b(32'h15a4e35), .out(multiplier_1_out));  // open: cin, cout
  Adder #(.width(32)) adder_1 (.a(multiplier_1_out), .b(32'h1), .out(adder_1_out));  // open: cin, cout
  Comparator #(.width(16), .mode("unsigned")) comparator_1 (.a(RNG), .b(Rate), .lt(Flip));  // open: gt, eq
  Register #(.width(32)) register_1 (.D(adder_1_out), .Q(SEED), .clk(CLK));  // open: en, clr
  assign RNG = SEED[15:0] ^ SEED[31:16];  // XOR_Gate xor_2, 16 bits wide
endmodule

module ClockDivisor (
  input  in_1,
  input  in_2,
  output out_3,
  output out_4,
  output out_5,
  output out_6,
  output out_7,
  output out_8,
  output out_9,
  output out_10,
  output out_11,
  output out_12,
  output out_13,
  output out_14,
  output out_15
);

  wire [12:0] bit_extender_1_out;

  Counter #(.width(4), .max('h2)) counter_1 (
    .carry(out_3), .clk(in_1), .clr(bit_extender_1_out[12]));  // open: load, D, count, Q
  Counter #(.width(4), .max('h3)) counter_2 (
    .carry(out_4), .clk(in_1), .clr(bit_extender_1_out[11]));  // open: load, D, count, Q
  Counter #(.width(4), .max('h5)) counter_3 (
    .carry(out_6), .clk(in_1), .clr(bit_extender_1_out[9]));  // open: load, D, count, Q
  Counter #(.width(4), .max('h4)) counter_4 (
    .carry(out_5), .clk(in_1), .clr(bit_extender_1_out[10]));  // open: load, D, count, Q
  Counter #(.width(4), .max('h6)) counter_5 (
    .carry(out_7), .clk(in_1), .clr(bit_extender_1_out[8]));  // open: load, D, count, Q
  Counter #(.width(4), .max('h7)) counter_6 (
    .carry(out_8), .clk(in_1), .clr(bit_extender_1_out[7]));  // open: load, D, count, Q
  Counter #(.width(4), .max('h8)) counter_7 (
    .carry(out_9), .clk(in_1), .clr(bit_extender_1_out[6]));  // open: load, D, count, Q
  Counter #(.width(4), .max('h9)) counter_8 (
    .carry(out_10), .clk(in_1), .clr(bit_extender_1_out[5]));  // open: load, D, count, Q
  assign bit_extender_1_out = {{12{in_2}}, in_2};  // Bit_Extender bit_extender_1
  Counter #(.width(4), .max('ha)) counter_9 (
    .carry(out_11), .clk(in_1), .clr(bit_extender_1_out[4]));  // open: load, D, count, Q
  Counter #(.width(4), .max('hb)) counter_10 (
    .carry(out_12), .clk(in_1), .clr(bit_extender_1_out[3]));  // open: load, D, count, Q
  Counter #(.width(4), .max('hc)) counter_11 (
    .carry(out_13), .clk(in_1), .clr(bit_extender_1_out[2]));  // open: load, D, count, Q
  Counter #(.width(4), .max('hd)) counter_12 (
    .carry(out_14), .clk(in_1), .clr(bit_extender_1_out[1]));  // open: load, D, count, Q
  Counter #(.width(4), .max('he)) counter_13 (
    .carry(out_15), .clk(in_1), .clr(bit_extender_1_out[0]));  // open: load, D, count, Q

  // Other names for the same wires on the sheet: CLK = in_1
endmodule

module BitStuffer (
  input  in_1,
  input  in_2,
  input  in_3
);

  wire controlled_buffer_1_out, controlled_buffer_2_out, d_ff_1_q, d_ff_2_q, d_ff_3_q, DisableSh,
       multiplexer_1_out, not_1_out, not_3_out, not_4_out, not_5_out, or_1_out, or_2_out,
       shift_register_1_out, StartStop;
  wire [1:0] counter_2_carry;

  not not_1 (not_1_out, DisableSh);
  Shift_Register shift_register_1 (
    .shift(not_1_out), .in(in_3), .clk(in_2), .out(shift_register_1_out));  // open: load, clr, d0, q0, d1, q1, d2, q2, d3, q3, d4, q4, d5, q5, d6, q6, d7, q7
  assign controlled_buffer_1_out = StartStop ? in_2 : 1'bz;  // Controlled_Buffer controlled_buffer_1
  D_Flip_Flop d_ff_1 (
    .clk(controlled_buffer_1_out), .D(controlled_buffer_2_out), .Q(d_ff_1_q));  // open: Qn, preset, en, reset
  not not_2 (StartStop, in_1);
  assign controlled_buffer_2_out = StartStop ? shift_register_1_out : 1'bz;  // Controlled_Buffer controlled_buffer_2
  not not_3 (not_3_out, d_ff_1_q);
  D_Flip_Flop d_ff_2 (.clk(in_2), .D(counter_2_carry[1]), .Q(d_ff_2_q));  // open: Qn, preset, en, reset
  Counter #(.width(3), .max('h4)) counter_1 (
    .count(d_ff_1_q), .carry(counter_2_carry[1]), .clk(in_2), .clr(or_1_out));  // open: load, D, Q
  or or_1 (or_1_out, d_ff_2_q, not_4_out);
  not not_4 (not_4_out, d_ff_1_q);
  not not_5 (not_5_out, counter_2_carry[1]);
  Counter #(.width(3), .max('h4)) counter_2 (
    .count(not_3_out), .carry(counter_2_carry[0]), .clk(in_2), .clr(or_2_out));  // open: load, D, Q
  or or_2 (or_2_out, d_ff_1_q, d_ff_3_q);
  or or_3 (DisableSh, counter_2_carry[1], counter_2_carry[0]);
  D_Flip_Flop d_ff_3 (.clk(in_2), .D(counter_2_carry[0]), .Q(d_ff_3_q));  // open: Qn, preset, en, reset
  Multiplexer #(.select(2)) multiplexer_1 (
    .in0(shift_register_1_out), .in1(counter_2_carry[0]), .in2(not_5_out), .out(multiplexer_1_out),
    .sel(counter_2_carry));  // open: in3, en
  Shift_Register shift_register_2 (
    .in(multiplexer_1_out), .clk(in_2));  // open: shift, out, load, clr, d0, q0, d1, q1, d2, q2, d3, q3, d4, q4, d5, q5, d6, q6, d7, q7

  // Other names for the same wires on the sheet: CLK = in_2; Input = in_3
endmodule

module FIFO (
  input  [21:0] in_1,
  input  [21:0] in_2,
  input  [21:0] in_3,
  input  [21:0] in_4,
  input  [21:0] in_5,
  input  [21:0] in_6,
  input  [21:0] in_7,
  input  [21:0] in_8,
  input  [21:0] in_9,
  input  [21:0] in_10,
  input  [21:0] in_11,
  input  [21:0] in_12,
  input  [21:0] in_13,
  input  [21:0] in_14,
  input  [21:0] in_15,
  input  [21:0] in_16,
  input  in_17,
  input  [21:0] in_18,
  output [21:0] out_19,
  output [21:0] out_20,
  output [21:0] out_21,
  output [21:0] out_22,
  output [21:0] out_23,
  output [21:0] out_24,
  output [21:0] out_25,
  output [21:0] out_26,
  output [21:0] out_27,
  output [21:0] out_28,
  output [21:0] out_29,
  output [21:0] out_30,
  output [21:0] out_31,
  output [21:0] out_32,
  output [21:0] out_33,
  output [21:0] out_34,
  output [21:0] out_35
);

  wire CLK;
  wire [21:0] multiplexer_1_out, multiplexer_2_out, multiplexer_3_out, multiplexer_4_out, multiplexer_5_out,
       multiplexer_6_out, multiplexer_7_out, multiplexer_8_out, multiplexer_9_out, multiplexer_10_out,
       multiplexer_11_out, multiplexer_12_out, multiplexer_13_out, multiplexer_14_out, multiplexer_15_out,
       multiplexer_16_out;

  Multiplexer #(.width(22)) multiplexer_1 (.in0(in_18), .in1(in_1), .out(multiplexer_1_out), .sel(in_17));  // open: en
  Register #(.width(22)) register_1 (.D(multiplexer_1_out), .Q(out_20), .clk(CLK));  // open: en, clr
  Multiplexer #(.width(22)) multiplexer_2 (.in0(out_20), .in1(in_2), .out(multiplexer_2_out), .sel(in_17));  // open: en
  Clock clock_1 (.out(CLK));
  Register #(.width(22)) register_2 (.D(multiplexer_2_out), .Q(out_21), .clk(CLK));  // open: en, clr
  Multiplexer #(.width(22)) multiplexer_3 (.in0(out_21), .in1(in_3), .out(multiplexer_3_out), .sel(in_17));  // open: en
  Register #(.width(22)) register_3 (.D(multiplexer_3_out), .Q(out_22), .clk(CLK));  // open: en, clr
  Multiplexer #(.width(22)) multiplexer_4 (.in0(out_22), .in1(in_4), .out(multiplexer_4_out), .sel(in_17));  // open: en
  Register #(.width(22)) register_4 (.D(multiplexer_4_out), .Q(out_23), .clk(CLK));  // open: en, clr
  Multiplexer #(.width(22)) multiplexer_5 (.in0(out_23), .in1(in_5), .out(multiplexer_5_out), .sel(in_17));  // open: en
  Multiplexer #(.width(22)) multiplexer_6 (.in0(out_24), .in1(in_6), .out(multiplexer_6_out), .sel(in_17));  // open: en
  Register #(.width(22)) register_5 (.D(multiplexer_5_out), .Q(out_24), .clk(CLK));  // open: en, clr
  Register #(.width(22)) register_6 (.D(multiplexer_6_out), .Q(out_25), .clk(CLK));  // open: en, clr
  Register #(.width(22)) register_7 (.D(multiplexer_7_out), .Q(out_26), .clk(CLK));  // open: en, clr
  Multiplexer #(.width(22)) multiplexer_7 (.in0(out_25), .in1(in_7), .out(multiplexer_7_out), .sel(in_17));  // open: en
  Register #(.width(22)) register_8 (.D(multiplexer_8_out), .Q(out_27), .clk(CLK));  // open: en, clr
  Multiplexer #(.width(22)) multiplexer_8 (.in0(out_26), .in1(in_8), .out(multiplexer_8_out), .sel(in_17));  // open: en
  Multiplexer #(.width(22)) multiplexer_9 (.in0(out_27), .in1(in_9), .out(multiplexer_9_out), .sel(in_17));  // open: en
  Register #(.width(22)) register_9 (.D(multiplexer_9_out), .Q(out_28), .clk(CLK));  // open: en, clr
  Multiplexer #(.width(22)) multiplexer_10 (
    .in0(out_28), .in1(in_10), .out(multiplexer_10_out), .sel(in_17));  // open: en
  Register #(.width(22)) register_10 (.D(multiplexer_10_out), .Q(out_29), .clk(CLK));  // open: en, clr
  Multiplexer #(.width(22)) multiplexer_11 (
    .in0(out_29), .in1(in_11), .out(multiplexer_11_out), .sel(in_17));  // open: en
  Register #(.width(22)) register_11 (.D(multiplexer_11_out), .Q(out_30), .clk(CLK));  // open: en, clr
  Multiplexer #(.width(22)) multiplexer_12 (
    .in0(out_30), .in1(in_12), .out(multiplexer_12_out), .sel(in_17));  // open: en
  Register #(.width(22)) register_12 (.D(multiplexer_12_out), .Q(out_31), .clk(CLK));  // open: en, clr
  Multiplexer #(.width(22)) multiplexer_13 (
    .in0(out_31), .in1(in_13), .out(multiplexer_13_out), .sel(in_17));  // open: en
  Multiplexer #(.width(22)) multiplexer_14 (
    .in0(out_32), .in1(in_14), .out(multiplexer_14_out), .sel(in_17));  // open: en
  Register #(.width(22)) register_13 (.D(multiplexer_13_out), .Q(out_32), .clk(CLK));  // open: en, clr
  Register #(.width(22)) register_14 (.D(multiplexer_14_out), .Q(out_33), .clk(CLK));  // open: en, clr
  Multiplexer #(.width(22)) multiplexer_15 (
    .in0(out_33), .in1(in_15), .out(multiplexer_15_out), .sel(in_17));  // open: en
  Register #(.width(22)) register_15 (.D(multiplexer_15_out), .Q(out_34), .clk(CLK));  // open: en, clr
  Multiplexer #(.width(22)) multiplexer_16 (
    .in0(out_34), .in1(in_16), .out(multiplexer_16_out), .sel(in_17));  // open: en
  Register #(.width(22)) register_16 (.D(multiplexer_16_out), .Q(out_19), .clk(CLK));  // open: en, clr

  assign out_35 = out_19;
endmodule
